# Fritzing sketch i2c backpack (saved by Fritzing 0.9.0b)

parts:
  NEOPIXEL1 = Neopixel Strip -- White (30/m)
  Raspberry_Pi1 = Raspberry Pi B rev2
  Part1 = Arduino Nano (Rev3.0) (ICSP)

nets:
  GND: NEOPIXEL1.GND, Raspberry_Pi1.GND, Part1.GND
  N1: NEOPIXEL1.Din, Part1.D6
  5V: NEOPIXEL1.+5V, Raspberry_Pi1.5V, Part1.5V
  N2: Raspberry_Pi1.GPIO_2, Part1.A4
  N3: Raspberry_Pi1.GPIO_3, Part1.A5

custom parts:
  Neopixel Strip -- White (30/m): These NeoPixel strips have 30 digitally-addressable pixel LEDs per meter and are very affordable and are only 12.5 mm wide, 10 mm if you remove the strip from the casing.
