# Fritzing sketch arduino_multipin (saved by Fritzing 0.9.2b)

parts:
  NEOPIXEL1 = Neopixel Strip -- White (30/m)
  Part1 = Arduino Uno (Rev3)
  NEOPIXEL2 = Neopixel Strip -- White (30/m)

nets:
  GND: NEOPIXEL1.GND, Part1.GND
  N1: NEOPIXEL1.Din, Part1.D9_PWM
  +5V: NEOPIXEL1.+5V, Part1.5V
  N2: Part1.D2, NEOPIXEL2.Din

custom parts:
  Neopixel Strip -- White (30/m): These NeoPixel strips have 30 digitally-addressable pixel LEDs per meter and are very affordable and are only 12.5 mm wide, 10 mm if you remove the strip from the casing.
  Arduino Uno (Rev3): The Arduino Uno is a microcontroller board based on the ATmega328 (datasheet). It has 14 digital input/output pins (of which 6 can be used as PWM outputs), 6 analog inputs, a 16 MHz ceramic resonator, a USB connection, a power jack, an ICSP header, and a reset button. It contains everything needed to support the microcontroller; simply connect it to a computer with a USB cable or power it with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
