# Fritzing sketch i2c_backpack_arduino_multipin (saved by Fritzing 0.9.2b)

parts:
  NEOPIXEL1 = Neopixel Strip -- White (30/m)
  Part1 = Arduino Nano (Rev3.0) (ICSP)
  Part2 = Arduino Uno (Rev3)
  NEOPIXEL2 = Neopixel Strip -- White (30/m)

nets:
  GND: NEOPIXEL1.GND, Part1.GND, Part2.GND
  N1: NEOPIXEL1.Din, Part1.D0/RX
  +5V: NEOPIXEL1.+5V, Part1.5V
  N2: Part1.D1/TX, NEOPIXEL2.Din
  N3: Part1.A5, Part2.A5/SCL
  N4: Part1.A4, Part2.A4/SDA

custom parts:
  Neopixel Strip -- White (30/m): These NeoPixel strips have 30 digitally-addressable pixel LEDs per meter and are very affordable and are only 12.5 mm wide, 10 mm if you remove the strip from the casing.
